# Fritzing sketch schematic (saved by Fritzing 0.9.2b)
breadboards: 1

parts:
  U1 = Arduino Nano (Rev3.0)
  U2 = mystery part, 6 pins [chip_label=RELAY]
  U3 = mystery part, 5 pins [chip_label="HUMID DET"]
  7~12V_DC_PWR = Power plug
  U4 = mystery part, 1 pin [chip_label=湿度传感器]
  VCC1 = 4 x AAA Battery Mount
  M1 = DC Motor

nets (from the schematic view):
  GND: U1.GND, U2.pin2, U3.pin2, 7~12V_DC_PWR.GND
  N1: U1.D11/MOSI, U3.pin3
  N2: U1.D12/MISO, U2.pin3
  VIN: U1.VIN, 7~12V_DC_PWR.VCC
  N3: U1.5V, U2.pin1, U3.pin1
  N4: U2.pin4, M1.pin_1
  N5: U2.pin5, VCC1.+
  N6: U3.pin5, U4.pin1
  N7: VCC1.-, M1.pin_2

notes:
  插入土壤中
